// Logisim project 2-bit Decoder.circ as structural Verilog
module _2_bit_Decoder (
  input  in_1,
  input  in_2,
  output out_3,
  output out_4,
  output out_5,
  output out_6
);

  wire not_1_out, not_2_out;

  not not_1 (not_1_out, in_1);
  not not_2 (not_2_out, in_2);
  and and_1 (out_3, not_1_out, not_2_out);
  and and_2 (out_4, in_1, not_2_out);
  and and_3 (out_5, in_2, not_1_out);
  and and_4 (out_6, in_2, in_1);
endmodule
