// Logisim project A1.circ as structural Verilog: 12 circuits, main circuit main
module main (
  output [3:0] out_1,
  output [3:0] out_2,
  output [3:0] out_3,
  output [3:0] out_4
);

  wire _2_bit_Decoder_out_3, _2_bit_Decoder_out_4, _2_bit_Decoder_out_5, _2_bit_Decoder_out_6, clock_1_out,
       not_1_out, not_2_out, not_3_out, not_4_out, not_5_out, R_Generator_out, random_1_out, random_2_out,
       random_3_out;
  wire [1:0] n2_bit_counter_1_out_2;
  wire [3:0] _4_bit__1_4_multiplexer_a, _4_bit__1_4_multiplexer_b, _4_bit__1_4_multiplexer_c,
       _4_bit__1_4_multiplexer_d, _4_bit__4_1_multiplexer_e, Shift_Register_2_q3, Shift_Register_3_q3,
       Shift_Register_4_q3, Shift_Register_q3;

  Random #(.width(1), .seed(111)) R_Generator (.clk(clock_1_out), .out(R_Generator_out));  // open: next, clr
  Random #(.width(1), .seed(231)) random_1 (.clk(clock_1_out), .out(random_1_out));  // open: next, clr
  Random #(.width(1), .seed(321)) random_2 (.clk(clock_1_out), .out(random_2_out));  // open: next, clr
  Random #(.width(1), .seed(65667)) random_3 (.clk(clock_1_out), .out(random_3_out));  // open: next, clr
  Shift_Register #(.length(4)) Shift_Register (
    .in(R_Generator_out), .clk(clock_1_out), .q0(Shift_Register_q3[3]), .q1(Shift_Register_q3[2]),
    .q2(Shift_Register_q3[1]), .q3(Shift_Register_q3[0]));  // open: shift, out, load, clr, d0, d1, d2, d3
  Shift_Register #(.length(4)) Shift_Register_2 (
    .in(random_1_out), .clk(clock_1_out), .q0(Shift_Register_2_q3[3]), .q1(Shift_Register_2_q3[2]),
    .q2(Shift_Register_2_q3[1]), .q3(Shift_Register_2_q3[0]));  // open: shift, out, load, clr, d0, d1, d2, d3
  Shift_Register #(.length(4)) Shift_Register_3 (
    .in(random_2_out), .clk(clock_1_out), .q0(Shift_Register_3_q3[3]), .q1(Shift_Register_3_q3[2]),
    .q2(Shift_Register_3_q3[1]), .q3(Shift_Register_3_q3[0]));  // open: shift, out, load, clr, d0, d1, d2, d3
  Shift_Register #(.length(4)) Shift_Register_4 (
    .in(random_3_out), .clk(clock_1_out), .q0(Shift_Register_4_q3[3]), .q1(Shift_Register_4_q3[2]),
    .q2(Shift_Register_4_q3[1]), .q3(Shift_Register_4_q3[0]));  // open: shift, out, load, clr, d0, d1, d2, d3
  Clock clock_1 (.out(clock_1_out));
  _2_bit_counter u_2_bit_counter_1 (.in_1(not_1_out), .out_2(n2_bit_counter_1_out_2));
  not not_1 (not_1_out, clock_1_out);
  _4bit__4_1_multiplexer _4_bit__4_1_multiplexer (
    .S1_S0(n2_bit_counter_1_out_2), .A(Shift_Register_q3), .B(Shift_Register_2_q3), .C(Shift_Register_3_q3),
    .D(Shift_Register_4_q3), .E(_4_bit__4_1_multiplexer_e));
  _4bit__1_4_De_Multiplexer _4_bit__1_4_multiplexer (
    .E(_4_bit__4_1_multiplexer_e), .S1_S0(n2_bit_counter_1_out_2), .A(_4_bit__1_4_multiplexer_a),
    .B(_4_bit__1_4_multiplexer_b), .C(_4_bit__1_4_multiplexer_c), .D(_4_bit__1_4_multiplexer_d));
  not not_2 (not_2_out, _2_bit_Decoder_out_3);
  not not_3 (not_3_out, _2_bit_Decoder_out_4);
  _2_bit_Decoder _2_bit_Decoder (
    .in_1(n2_bit_counter_1_out_2[0]), .in_2(n2_bit_counter_1_out_2[1]), .out_3(_2_bit_Decoder_out_3),
    .out_4(_2_bit_Decoder_out_4), .out_5(_2_bit_Decoder_out_5), .out_6(_2_bit_Decoder_out_6));
  _4bit_Register _4_bit_Register (.In(_4_bit__1_4_multiplexer_a), .Clock(not_2_out), .Out(out_1));
  _4bit_Register _4_bit_Register_2 (.In(_4_bit__1_4_multiplexer_b), .Clock(not_3_out), .Out(out_2));
  _4bit_Register _4_bit_Register_3 (.In(_4_bit__1_4_multiplexer_c), .Clock(not_4_out), .Out(out_3));
  _4bit_Register _4_bit_Register_4 (.In(_4_bit__1_4_multiplexer_d), .Clock(not_5_out), .Out(out_4));
  not not_4 (not_4_out, _2_bit_Decoder_out_5);
  not not_5 (not_5_out, _2_bit_Decoder_out_6);
endmodule

module _2_bit_Decoder (
  input  in_1,
  input  in_2,
  output out_3,
  output out_4,
  output out_5,
  output out_6
);

  wire not_1_out, not_2_out;

  not not_1 (not_1_out, in_1);
  not not_2 (not_2_out, in_2);
  and and_1 (out_3, not_1_out, not_2_out);
  and and_2 (out_4, in_1, not_2_out);
  and and_3 (out_5, in_2, not_1_out);
  and and_4 (out_6, in_2, in_1);
endmodule

module _4_bit_Activator (
  input  Enable,
  input  [3:0] In,
  output [3:0] Out
);

  and and_1 (Out[0], In[0], Enable);
  and and_2 (Out[1], In[1], Enable);
  and and_3 (Out[2], In[2], Enable);
  and and_4 (Out[3], In[3], Enable);

  // Notes on the sheet:
  //   Enable: pull=down
endmodule

module Multiplexers (
  input  [1:0] Select,
  input  [3:0] In_0,
  input  [3:0] In_1,
  input  [3:0] In_2,
  input  [3:0] In_3,
  output [3:0] Out
);

  wire n2_bit_decoder_1_out_3, n2_bit_decoder_1_out_4, n2_bit_decoder_1_out_5, n2_bit_decoder_1_out_6;
  wire [3:0] n4_bit_activator_1_out, n4_bit_activator_2_out, n4_bit_activator_3_out, n4_bit_activator_4_out;

  _2_bit_Decoder u_2_bit_decoder_1 (
    .in_1(Select[0]), .in_2(Select[1]), .out_3(n2_bit_decoder_1_out_3), .out_4(n2_bit_decoder_1_out_4),
    .out_5(n2_bit_decoder_1_out_5), .out_6(n2_bit_decoder_1_out_6));
  _4_bit_Activator u_4_bit_activator_1 (.In(In_0), .Enable(n2_bit_decoder_1_out_3), .Out(n4_bit_activator_1_out));
  _4_bit_Activator u_4_bit_activator_2 (.In(In_1), .Enable(n2_bit_decoder_1_out_4), .Out(n4_bit_activator_2_out));
  _4_bit_Activator u_4_bit_activator_3 (.In(In_2), .Enable(n2_bit_decoder_1_out_5), .Out(n4_bit_activator_3_out));
  _4_bit_Activator u_4_bit_activator_4 (.In(In_3), .Enable(n2_bit_decoder_1_out_6), .Out(n4_bit_activator_4_out));
  assign Out = n4_bit_activator_1_out | n4_bit_activator_2_out | n4_bit_activator_3_out | n4_bit_activator_4_out;  // OR_Gate or_1, 4 bits wide
endmodule

module D_Latch (
  input  D,
  input  E,
  output minus_Q,
  output Q
);

  wire and_1_out, and_2_out, not_1_out;

  not not_1 (not_1_out, D);
  and and_1 (and_1_out, D, E);
  and and_2 (and_2_out, E, not_1_out);
  nor nor_1 (minus_Q, and_1_out, Q);
  nor nor_2 (Q, minus_Q, and_2_out);

  // Notes on the sheet:
  //   D: pull=down
  //   minus_Q: pull=down
  //   Q: pull=down
  //   E: pull=down
endmodule

module D_FlipFlop (
  input  D,
  input  C,
  output minus_Q,
  output Q
);

  wire d_latch_1_q, not_1_out;

  D_Latch d_latch_1 (.D(D), .E(not_1_out), .Q(d_latch_1_q));  // open: minus_Q
  not not_1 (not_1_out, C);
  D_Latch d_latch_2 (.D(d_latch_1_q), .E(C), .minus_Q(minus_Q), .Q(Q));
endmodule

module _2bit_Decoder (
  input  In_0,
  input  In_1,
  output Select_0,
  output Select_1,
  output Select_2,
  output Select_3
);

  wire not_1_out, not_2_out;

  not not_1 (not_1_out, In_0);
  not not_2 (not_2_out, In_1);
  and and_1 (Select_0, not_1_out, not_2_out);
  and and_2 (Select_1, In_0, not_2_out);
  and and_3 (Select_2, In_1, not_1_out);
  and and_4 (Select_3, In_0, In_1);

  // Notes on the sheet:
  //   In_1: pull=down
  //   In_0: pull=down
endmodule

module Latches_and_FlipFlops (
  input  [3:0] Data_In,
  input  Select_0,
  input  Select_1,
  input  Clock,
  output [3:0] Reg_0_Value,
  output [3:0] Reg_1_Value,
  output [3:0] Reg_2_Value,
  output [3:0] Reg_3_Value
);

  wire and_1_out, and_2_out, and_3_out, and_4_out, n2bit_decoder_1_select_0, n2bit_decoder_1_select_1,
       n2bit_decoder_1_select_2, n2bit_decoder_1_select_3;

  _2bit_Decoder u_2bit_decoder_1 (
    .In_0(Select_0), .In_1(Select_1), .Select_0(n2bit_decoder_1_select_0),
    .Select_1(n2bit_decoder_1_select_1), .Select_2(n2bit_decoder_1_select_2),
    .Select_3(n2bit_decoder_1_select_3));
  and and_1 (and_1_out, n2bit_decoder_1_select_0, Clock);
  and and_2 (and_2_out, n2bit_decoder_1_select_1, Clock);
  and and_3 (and_3_out, n2bit_decoder_1_select_2, Clock);
  and and_4 (and_4_out, n2bit_decoder_1_select_3, Clock);
  _4bit_Register FlipFlop_0 (.In(Data_In), .Clock(and_1_out), .Out(Reg_0_Value));
  _4bit_Register FlipFlop_1 (.In(Data_In), .Clock(and_2_out), .Out(Reg_1_Value));
  _4bit_Register FlipFlop_2 (.In(Data_In), .Clock(and_3_out), .Out(Reg_2_Value));
  _4bit_Register FlipFlop_3 (.In(Data_In), .Clock(and_4_out), .Out(Reg_3_Value));
endmodule

module _4bit__4_1_multiplexer (
  input  [1:0] S1_S0,
  input  [3:0] A,
  input  [3:0] B,
  input  [3:0] C,
  input  [3:0] D,
  output [3:0] E
);

  wire n2_bit_decoder_1_out_3, n2_bit_decoder_1_out_4, n2_bit_decoder_1_out_5, n2_bit_decoder_1_out_6;
  wire [3:0] n4_bit_activator_1_out, n4_bit_activator_2_out, n4_bit_activator_3_out, n4_bit_activator_4_out;

  _2_bit_Decoder u_2_bit_decoder_1 (
    .in_1(S1_S0[0]), .in_2(S1_S0[1]), .out_3(n2_bit_decoder_1_out_3), .out_4(n2_bit_decoder_1_out_4),
    .out_5(n2_bit_decoder_1_out_5), .out_6(n2_bit_decoder_1_out_6));
  _4_bit_Activator u_4_bit_activator_1 (.In(A), .Enable(n2_bit_decoder_1_out_3), .Out(n4_bit_activator_1_out));
  _4_bit_Activator u_4_bit_activator_2 (.In(B), .Enable(n2_bit_decoder_1_out_4), .Out(n4_bit_activator_2_out));
  _4_bit_Activator u_4_bit_activator_3 (.In(C), .Enable(n2_bit_decoder_1_out_5), .Out(n4_bit_activator_3_out));
  _4_bit_Activator u_4_bit_activator_4 (.In(D), .Enable(n2_bit_decoder_1_out_6), .Out(n4_bit_activator_4_out));
  assign E = n4_bit_activator_1_out | n4_bit_activator_2_out | n4_bit_activator_3_out | n4_bit_activator_4_out;  // OR_Gate or_1, 4 bits wide
endmodule

module _4bit__1_4_De_Multiplexer (
  input  [3:0] E,
  input  [1:0] S1_S0,
  output [3:0] A,
  output [3:0] B,
  output [3:0] C,
  output [3:0] D
);

  wire n2_bit_decoder_1_out_3, n2_bit_decoder_1_out_4, n2_bit_decoder_1_out_5, n2_bit_decoder_1_out_6;

  _4_bit_Activator u_4_bit_activator_1 (.In(E), .Enable(n2_bit_decoder_1_out_3), .Out(A));
  _4_bit_Activator u_4_bit_activator_2 (.In(E), .Enable(n2_bit_decoder_1_out_4), .Out(B));
  _4_bit_Activator u_4_bit_activator_3 (.In(E), .Enable(n2_bit_decoder_1_out_5), .Out(C));
  _4_bit_Activator u_4_bit_activator_4 (.In(E), .Enable(n2_bit_decoder_1_out_6), .Out(D));
  _2_bit_Decoder u_2_bit_decoder_1 (
    .in_1(S1_S0[0]), .in_2(S1_S0[1]), .out_3(n2_bit_decoder_1_out_3), .out_4(n2_bit_decoder_1_out_4),
    .out_5(n2_bit_decoder_1_out_5), .out_6(n2_bit_decoder_1_out_6));
endmodule

module _4bit_Register (
  input  [3:0] In,
  input  Clock,
  output [3:0] Out
);

  D_FlipFlop d_flipflop_1 (.D(In[0]), .C(Clock), .Q(Out[0]));  // open: minus_Q
  D_FlipFlop d_flipflop_2 (.D(In[1]), .C(Clock), .Q(Out[1]));  // open: minus_Q
  D_FlipFlop d_flipflop_3 (.D(In[2]), .C(Clock), .Q(Out[2]));  // open: minus_Q
  D_FlipFlop d_flipflop_4 (.D(In[3]), .C(Clock), .Q(Out[3]));  // open: minus_Q
endmodule

module _2_bit_counter (
  input  in_1,
  output [1:0] out_2
);

  wire d_flipflop_1_minus_q, d_flipflop_2_minus_q;

  D_FlipFlop d_flipflop_1 (.D(d_flipflop_1_minus_q), .C(in_1), .minus_Q(d_flipflop_1_minus_q), .Q(out_2[0]));
  D_FlipFlop d_flipflop_2 (
    .D(d_flipflop_2_minus_q), .C(d_flipflop_1_minus_q), .minus_Q(d_flipflop_2_minus_q), .Q(out_2[1]));
endmodule
