// Logisim project Latches and FlipFlops - Exercise 2.circ as structural Verilog: 5 circuits, main circuit main
module main (
  input  [3:0] Data_In,
  input  Select_0,
  input  Select_1,
  input  Clock,
  output [3:0] Reg_0_Value,
  output [3:0] Reg_1_Value,
  output [3:0] Reg_2_Value,
  output [3:0] Reg_3_Value
);

  wire and_1_out, and_2_out, and_3_out, and_4_out, n2bit_decoder_1_select_0, n2bit_decoder_1_select_1,
       n2bit_decoder_1_select_2, n2bit_decoder_1_select_3;

  _2bit_Decoder u_2bit_decoder_1 (
    .In_0(Select_0), .In_1(Select_1), .Select_0(n2bit_decoder_1_select_0),
    .Select_1(n2bit_decoder_1_select_1), .Select_2(n2bit_decoder_1_select_2),
    .Select_3(n2bit_decoder_1_select_3));
  and and_1 (and_1_out, n2bit_decoder_1_select_0, Clock);
  and and_2 (and_2_out, n2bit_decoder_1_select_1, Clock);
  and and_3 (and_3_out, n2bit_decoder_1_select_2, Clock);
  and and_4 (and_4_out, n2bit_decoder_1_select_3, Clock);
  _4bit_Register FlipFlop_0 (.In(Data_In), .Out(Reg_0_Value), .Clock(and_1_out));
  _4bit_Register FlipFlop_1 (.In(Data_In), .Out(Reg_1_Value), .Clock(and_2_out));
  _4bit_Register FlipFlop_2 (.In(Data_In), .Out(Reg_2_Value), .Clock(and_3_out));
  _4bit_Register FlipFlop_3 (.In(Data_In), .Out(Reg_3_Value), .Clock(and_4_out));
endmodule

module D_Latch (
  input  D,
  input  E,
  output minus_Q,
  output Q
);

  wire and_1_out, and_2_out, not_1_out;

  not not_1 (not_1_out, D);
  and and_1 (and_1_out, D, E);
  and and_2 (and_2_out, E, not_1_out);
  nor nor_1 (minus_Q, and_1_out, Q);
  nor nor_2 (Q, minus_Q, and_2_out);

  // Notes on the sheet:
  //   Q: pull=down
  //   D: pull=down
  //   minus_Q: pull=down
  //   E: pull=down
endmodule

module D_FlipFlop__pos_edge (
  input  D,
  input  C,
  output Q
);

  wire d_latch_1_q, not_1_out;

  D_Latch d_latch_1 (.D(D), .E(not_1_out), .Q(d_latch_1_q));  // open: minus_Q
  not not_1 (not_1_out, C);
  D_Latch d_latch_2 (.D(d_latch_1_q), .E(C), .Q(Q));  // open: minus_Q
endmodule

module _4bit_Register (
  input  [3:0] In,
  input  Clock,
  output [3:0] Out
);

  D_FlipFlop__pos_edge d_flipflop_pos_edge_1 (.D(In[0]), .C(Clock), .Q(Out[0]));
  D_FlipFlop__pos_edge d_flipflop_pos_edge_2 (.D(In[1]), .C(Clock), .Q(Out[1]));
  D_FlipFlop__pos_edge d_flipflop_pos_edge_3 (.D(In[2]), .C(Clock), .Q(Out[2]));
  D_FlipFlop__pos_edge d_flipflop_pos_edge_4 (.D(In[3]), .C(Clock), .Q(Out[3]));
endmodule

module _2bit_Decoder (
  input  In_0,
  input  In_1,
  output Select_0,
  output Select_1,
  output Select_2,
  output Select_3
);

  wire not_1_out, not_2_out;

  not not_1 (not_1_out, In_0);
  not not_2 (not_2_out, In_1);
  and and_1 (Select_0, not_1_out, not_2_out);
  and and_2 (Select_1, In_0, not_2_out);
  and and_3 (Select_2, In_1, not_1_out);
  and and_4 (Select_3, In_0, In_1);

  // Notes on the sheet:
  //   In_0: pull=down
  //   In_1: pull=down
endmodule
