// Logisim project Multiplexers - Exercise.circ as structural Verilog: 3 circuits, main circuit main
module main (
  input  [1:0] Select,
  input  [3:0] In_0,
  input  [3:0] In_1,
  input  [3:0] In_2,
  input  [3:0] In_3,
  output [3:0] Out
);

  wire n2bit_decoder_1_select_0, n2bit_decoder_1_select_1, n2bit_decoder_1_select_2, n2bit_decoder_1_select_3;
  wire [3:0] n4bit_activator_1_out, n4bit_activator_2_out, n4bit_activator_3_out, n4bit_activator_4_out;

  _2bit_Decoder u_2bit_decoder_1 (
    .In_0(Select[0]), .In_1(Select[1]), .Select_0(n2bit_decoder_1_select_0),
    .Select_1(n2bit_decoder_1_select_1), .Select_2(n2bit_decoder_1_select_2),
    .Select_3(n2bit_decoder_1_select_3));
  _4Bit_Activator u_4bit_activator_1 (.In(In_0), .Out(n4bit_activator_1_out), .Enable(n2bit_decoder_1_select_0));
  _4Bit_Activator u_4bit_activator_2 (.In(In_1), .Out(n4bit_activator_2_out), .Enable(n2bit_decoder_1_select_1));
  _4Bit_Activator u_4bit_activator_3 (.In(In_2), .Out(n4bit_activator_3_out), .Enable(n2bit_decoder_1_select_2));
  _4Bit_Activator u_4bit_activator_4 (.In(In_3), .Out(n4bit_activator_4_out), .Enable(n2bit_decoder_1_select_3));
  assign Out = n4bit_activator_1_out | n4bit_activator_2_out | n4bit_activator_3_out | n4bit_activator_4_out;  // OR_Gate or_1, 4 bits wide
endmodule

module _2bit_Decoder (
  input  In_0,
  input  In_1,
  output Select_0,
  output Select_1,
  output Select_2,
  output Select_3
);

  wire not_1_out, not_2_out;

  not not_1 (not_1_out, In_0);
  not not_2 (not_2_out, In_1);
  and and_1 (Select_0, not_1_out, not_2_out);
  and and_2 (Select_1, In_0, not_2_out);
  and and_3 (Select_2, In_1, not_1_out);
  and and_4 (Select_3, In_0, In_1);

  // Notes on the sheet:
  //   In_0: pull=down
  //   In_1: pull=down
endmodule

module _4Bit_Activator (
  input  Enable,
  input  [3:0] In,
  output [3:0] Out
);

  and and_1 (Out[0], In[0], Enable);
  and and_2 (Out[1], In[1], Enable);
  and and_3 (Out[2], In[2], Enable);
  and and_4 (Out[3], In[3], Enable);

  // Notes on the sheet:
  //   Enable: pull=down
endmodule
