// Logisim project dsadsa.circ as structural Verilog: 1 circuit, main circuit main
module main (
  input  in_1,
  input  in_2,
  input  in_3,
  input  in_4,
  input  in_5,
  input  in_6,
  input  in_7,
  input  in_8,
  output out_9,
  output out_10,
  output out_11,
  output out_12,
  output out_13,
  output out_14,
  output out_15,
  output out_16
);

  wire and_1_out, and_2_out, and_3_out, and_4_out, and_5_out, and_6_out, and_7_out, and_8_out, not_1_out,
       not_2_out, not_3_out, not_4_out;

  not not_1 (not_1_out, in_1);
  not not_2 (not_2_out, in_3);
  not not_3 (not_3_out, in_5);
  not not_4 (not_4_out, in_7);
  and and_1 (and_1_out, in_1, in_2);
  and and_2 (and_2_out, in_2, not_1_out);
  and and_3 (and_3_out, in_3, in_4);
  and and_4 (and_4_out, in_4, not_2_out);
  and and_5 (and_5_out, in_5, in_6);
  and and_6 (and_6_out, in_6, not_3_out);
  and and_7 (and_7_out, in_7, in_8);
  and and_8 (and_8_out, in_8, not_4_out);
  nor nor_1 (out_9, and_1_out, out_10);
  nor nor_2 (out_10, out_9, and_2_out);
  nor nor_3 (out_11, and_3_out, out_12);
  nor nor_4 (out_12, out_11, and_4_out);
  nor nor_5 (out_13, and_5_out, out_14);
  nor nor_6 (out_14, out_13, and_6_out);
  nor nor_7 (out_15, and_7_out, out_16);
  nor nor_8 (out_16, out_15, and_8_out);
endmodule
